# Fritzing sketch Ex2 (saved by Fritzing 0.9.2b)
breadboards: 1

parts:
  R2 = Resistor [tolerance=±5% resistance=10k package=THT]
  KEY = Pushbutton [package="[THT]"]
  Part1 = Arduino Nano (Rev3.0)
  LED1 = LED - 5mm [color="Red (633nm)" package="5 mm [THT]"]

nets:
  N1: R2.Pin_0, Part1.GND, LED1.cathode
  N2: R2.Pin_1, KEY.Pin_3, KEY.Pin_4, Part1.D4
  N3: KEY.Pin_1, KEY.Pin_2, Part1.3V3
  N4: Part1.D3, LED1.anode
