# Fritzing sketch ex5 (saved by Fritzing 0.9.2b)
breadboards: 1

parts:
  元件1 = Arduino Uno (Rev3)
  LCD1602 = LCD screen
  R4 = Rotary Potentiometer (Small) [maximum_resistance=100kΩ package=THT]

nets:
  N1: 元件1.D10_PWM/SS, LCD1602.DB4
  N2: 元件1.D11_PWM/MOSI, LCD1602.DB5
  N3: 元件1.D12/MISO, LCD1602.DB6
  N4: 元件1.D13/SCK, LCD1602.DB7
  GND: 元件1.GND, LCD1602.VSS, LCD1602.R/W, LCD1602.LED-, R4.leg1
  N5: 元件1.D4, LCD1602.RS
  N6: 元件1.D6_PWM, LCD1602.E
  N7: 元件1.3V3, LCD1602.LED+
  5V: 元件1.5V, LCD1602.VDD, R4.leg2
  N8: LCD1602.V0, R4.wiper
