# Fritzing sketch ex7 (saved by Fritzing 0.9.2b)

parts:
  OLED1 = 128x32 I2C Monochrome OLED Display
  Part1 = Arduino Mega 2560 (Rev3)

nets:
  N1: OLED1.SDA, Part1.D20/SDA
  N2: OLED1.SCL, Part1.D21/SCL
  GND: OLED1.GND, Part1.GND
  3.3V: OLED1.3.3V, Part1.3V3
