# Fritzing sketch ex8 (saved by Fritzing 0.9.2b)
breadboards: 2

parts:
  J1 = female pin header, 2 pins [form="♀ (female)"]
  J2 = female pin header, 2 pins [form="♀ (female)"]
  J3 = female pin header, 2 pins [form="♀ (female)"]
  CONN1 = USB connector [package=THT]
  J4 = female pin header, 2 pins [form="♀ (female)"]
  J5 = female pin header, 2 pins [form="♀ (female)"]
  J6 = female pin header, 2 pins [form="♀ (female)"]
  S1 = Pushbutton [package="[THT]"]

nets:
  N1: J1.pin1, J2.pin1
  N2: J1.pin2, J2.pin2, S1.Pin_3, S1.Pin_4
  N3: J3.pin1, J3.pin2
  N4: CONN1.GND, CONN1.chassis5, CONN1.chassis6
  N5: J4.pin1, J4.pin2, J5.pin1
  N6: J6.pin2, S1.Pin_1, S1.Pin_2
