# Fritzing sketch ex9 (saved by Fritzing 0.9.2b)
breadboards: 1

parts:
  U1 = atmega168 [package=dip]
  XTAL1 = Crystal [frequency="16 Mhz" package=THT]
  S1 = Pushbutton [package="[THT]"]
  Part1 = FTDI Basic Programmer
  LED1 = LED - 5mm [color="Red (633nm)" package="5 mm [THT]"]

nets:
  N1: U1.RESET, S1.Pin_1, S1.Pin_2
  N2: U1.D0_(RX), Part1.TXO
  N3: U1.D1_(TX), Part1.RXI
  N4: U1.VCC, Part1.POWER
  N5: U1.GND#7, S1.Pin_3, S1.Pin_4, Part1.GND, LED1.cathode
  N6: U1.XLAT1, XTAL1.pin_0
  N7: U1.XLAT2, XTAL1.pin_1
  N8: U1.D13, LED1.anode
