# Fritzing sketch circuit (saved by Fritzing 0.9.2b)
breadboards: 1

parts:
  Raspberry_Pi1 = Raspberry Pi 2
  LED1 = LED - 5mm [color="Red (633nm)" package="5 mm [THT]"]
  T1 = LM35 Temperature Sensor [package="TO92 [THT]"]

nets:
  3V3: Raspberry_Pi1.3v3, Raspberry_Pi1.3V3, T1.+Vs
  N1: Raspberry_Pi1.GPIO17, T1.Vout
  GND: Raspberry_Pi1.GND, LED1.cathode, T1.GND
  N2: Raspberry_Pi1.GPIO18, LED1.anode
